// Logisim project Guess_The_Number_Xtreme.circ as structural Verilog: 9 circuits, main circuit main
// x
module main (
  input  in_1,
  input  in_2,
  input  in_3,
  input  in_4,
  input  in_5,
  input  in_6,
  input  in_7,
  input  in_8
);

  wire A_JOGANDO, A_VENCEU, ACERTOU, B_JOGANDO, B_VENCEU, CHUTANDO_X, CHUTANDO_Y, chutar, CONFIGURAR, EMPATE,
       FIM_DE_JOGO, IGUAL, MAIOR, MENOR, proximo, RESET, SA, SB, START, SX, SY, tunnel;
  wire [3:0] GA, GB, XH, YH;

  Button button_1 ();  // open: out
  Button button_2 ();  // open: out
  Hex_Digit_Display hex_digit_display_1 ();  // open: value, dp
  Hex_Digit_Display hex_digit_display_2 ();  // open: value, dp
  LED led_1 (.in(SA));
  Hex_Digit_Display hex_digit_display_3 ();  // open: value, dp
  Button button_3 ();  // open: out
  LED #(.active("false")) led_2 ();  // open: in
  LED #(.active("false")) led_3 ();  // open: in
  Hex_Digit_Display hex_digit_display_4 ();  // open: value, dp
  Hex_Digit_Display hex_digit_display_5 (.value(GA));  // open: dp
  LED led_4 (.in(A_JOGANDO));
  Button button_4 ();  // open: out
  Hex_Digit_Display hex_digit_display_6 ();  // open: value, dp
  LED led_5 (.in(SX));
  LED led_6 (.in(A_VENCEU));
  Button button_5 (.out(START));
  LED led_7 (.in(MAIOR));
  Button button_6 (.out(proximo));
  Hex_Digit_Display hex_digit_display_7 (.value(XH));  // open: dp
  LED led_8 (.in(CHUTANDO_X));
  LED led_9 (.in(FIM_DE_JOGO));
  LED led_10 (.in(EMPATE));
  LED led_11 (.in(tunnel));
  Button button_7 (.out(CONFIGURAR));
  LED led_12 (.in(ACERTOU));
  LED led_13 (.in(IGUAL));
  Button button_8 (.out(chutar));
  LED led_14 (.in(SY));
  Hex_Digit_Display hex_digit_display_8 (.value(YH));  // open: dp
  LED led_15 (.in(CHUTANDO_Y));
  LED led_16 (.in(B_VENCEU));
  Button button_9 (.out(RESET));
  LED led_17 (.in(MENOR));
  Hex_Digit_Display hex_digit_display_9 ();  // open: value, dp
  Hex_Digit_Display hex_digit_display_10 ();  // open: value, dp
  LED #(.active("false")) led_18 ();  // open: in
  LED #(.active("false")) led_19 ();  // open: in
  Hex_Digit_Display hex_digit_display_11 ();  // open: value, dp
  LED led_20 (.in(SB));
  Hex_Digit_Display hex_digit_display_12 (.value(GB));  // open: dp
  LED led_21 (.in(B_JOGANDO));
  Hex_Digit_Display hex_digit_display_13 ();  // open: value, dp
  Hex_Digit_Display hex_digit_display_14 ();  // open: value, dp
  // Coordenadas coordenadas_1: pin names not known; wires that end beside it: proximo, chutar, A_JOGANDO, B_JOGANDO, GA, CHUTANDO_X, GB, CHUTANDO_Y, SX, SY, MAIOR, IGUAL, MENOR, XH, YH
  numero_negativo Jogador_A (
    .Entrada_3(in_1), .Entrada_2(in_2), .Entrada_1(in_3), .Entrada_0(in_4), .negativo(SA), .\Saída (GA));
  numero_negativo Jogador_B (
    .Entrada_3(in_5), .Entrada_2(in_6), .Entrada_1(in_7), .Entrada_0(in_8), .negativo(SB), .\Saída (GB));

  // Other names for the same wires on the sheet: A0 = in_4; A1 = in_3; A2 = in_2; A3 = in_1; B0 = in_8; B1 = in_7;
  //   B2 = in_6; B3 = in_5
endmodule

module Flip_Flop_SR (
  input  S_R,
  input  Clock,
  input  Preset,
  input  Enable,
  input  Clear,
  output out_6
);

  wire not_1_out;

  not not_1 (not_1_out, S_R);
  S_R_Flip_Flop s_r_ff_1 (
    .S(S_R), .clk(Clock), .R(not_1_out), .Q(out_6), .preset(Preset), .reset(Clear), .en(Enable));  // open: Qn
endmodule

module Decrementador (
  input  Clock,
  input  Preset,
  input  Enable,
  input  Clear,
  input  [3:0] valor_retorno,
  output [3:0] out_6
);

  wire comparator_1_eq;
  wire [3:0] adder_1_out, multiplexer_1_out;

  Hex_Digit_Display hex_digit_display_1 (.value(out_6));  // open: dp
  Flip_Flop_SR flip_flop_sr_1 (
    .S_R(multiplexer_1_out[3]), .Clock(Clock), .Preset(Preset), .Enable(Enable), .Clear(Clear),
    .out_6(out_6[3]));
  Flip_Flop_SR flip_flop_sr_2 (
    .S_R(multiplexer_1_out[2]), .Clock(Clock), .Preset(Preset), .Enable(Enable), .Clear(Clear),
    .out_6(out_6[2]));
  Flip_Flop_SR flip_flop_sr_3 (
    .S_R(multiplexer_1_out[1]), .Clock(Clock), .Preset(Preset), .Enable(Enable), .Clear(Clear),
    .out_6(out_6[1]));
  Multiplexer #(.width(4)) multiplexer_1 (
    .in0(adder_1_out), .in1(valor_retorno), .out(multiplexer_1_out), .sel(comparator_1_eq));  // open: en
  Flip_Flop_SR flip_flop_sr_4 (
    .S_R(multiplexer_1_out[0]), .Clock(Clock), .Preset(Preset), .Enable(Enable), .Clear(Clear),
    .out_6(out_6[0]));
  Hex_Digit_Display hex_digit_display_2 (.value(adder_1_out));  // open: dp
  Adder #(.width(4)) adder_1 (.a(out_6), .b(4'b1111), .out(adder_1_out));  // open: cin, cout
  Comparator #(.width(4)) comparator_1 (.a(adder_1_out), .b(4'b1111), .eq(comparator_1_eq));  // open: gt, lt
endmodule

module Verificador_9 (
  input  Enable
);

  wire and_1_out, clock_1_out, comparator_1_eq, comparator_2_eq, comparator_3_eq, comparator_4_eq, not_1_out;
  wire [3:0] and_2_out, decrementador_1_out_6, decrementador_2_out_6, decrementador_3_out_6,
       decrementador_4_out_6;

  and and_1 (and_1_out, Enable, not_1_out);
  not not_1 (not_1_out, comparator_2_eq);
  Hex_Digit_Display hex_digit_display_1 (.value(decrementador_1_out_6));  // open: dp
  Decrementador decrementador_1 (
    .Clock(comparator_1_eq), .Enable(and_1_out), .valor_retorno(4'b0101), .out_6(decrementador_1_out_6));  // open: Preset, Clear
  Hex_Digit_Display hex_digit_display_2 (.value(decrementador_2_out_6));  // open: dp
  Decrementador decrementador_2 (
    .Clock(comparator_3_eq), .Enable(and_1_out), .valor_retorno(4'b1001), .out_6(decrementador_2_out_6));  // open: Preset, Clear
  Comparator #(.width(4)) comparator_1 (.a(decrementador_2_out_6), .b(4'b1001), .eq(comparator_1_eq));  // open: gt, lt
  assign and_2_out = ~decrementador_1_out_6 & ~decrementador_2_out_6 & ~decrementador_3_out_6 & ~decrementador_4_out_6;  // AND_Gate and_2, 4 bits wide
  Hex_Digit_Display hex_digit_display_3 (.value(decrementador_3_out_6));  // open: dp
  Decrementador decrementador_3 (
    .Clock(comparator_4_eq), .Enable(and_1_out), .valor_retorno(4'b0101), .out_6(decrementador_3_out_6));  // open: Preset, Clear
  Comparator #(.width(4)) comparator_2 (.a(and_2_out), .b(4'b1111), .eq(comparator_2_eq));  // open: gt, lt
  Comparator #(.width(4)) comparator_3 (.a(decrementador_3_out_6), .b(4'b0101), .eq(comparator_3_eq));  // open: gt, lt
  Hex_Digit_Display hex_digit_display_4 (.value(decrementador_4_out_6));  // open: dp
  Decrementador decrementador_4 (
    .Clock(clock_1_out), .Enable(and_1_out), .valor_retorno(4'b1001), .out_6(decrementador_4_out_6));  // open: Preset, Clear
  Comparator #(.width(4)) comparator_4 (.a(decrementador_4_out_6), .b(4'b1001), .eq(comparator_4_eq));  // open: gt, lt
  Clock clock_1 (.out(clock_1_out));
endmodule

module decrementar_min_sec (
  input  Clear,
  input  Enable
);

  wire and_2_out, button_1_out, button_2_out, button_3_out, button_4_out, clock_1_out, comparator_1_eq,
       comparator_2_eq, comparator_3_eq, comparator_4_eq, multiplexer_1_out, multiplexer_2_out,
       multiplexer_3_out, multiplexer_4_out, not_1_out, not_2_out, or_1_out, or_2_out, or_3_out, or_4_out;
  wire [3:0] and_1_out, decrementador_1_out_6, decrementador_2_out_6, decrementador_3_out_6,
       decrementador_4_out_6;

  not not_1 (not_1_out, Enable);
  Hex_Digit_Display hex_digit_display_1 (.value(decrementador_1_out_6));  // open: dp
  Decrementador decrementador_1 (
    .Clock(multiplexer_1_out), .Enable(or_1_out), .Clear(Clear), .valor_retorno(4'b0101),
    .out_6(decrementador_1_out_6));  // open: Preset
  or or_1 (or_1_out, Enable, not_1_out);
  Multiplexer multiplexer_1 (
    .in0(button_1_out), .in1(comparator_1_eq), .out(multiplexer_1_out), .sel(Enable));  // open: en
  Button button_1 (.out(button_1_out));
  Hex_Digit_Display hex_digit_display_2 (.value(decrementador_2_out_6));  // open: dp
  Decrementador decrementador_2 (
    .Clock(multiplexer_2_out), .Enable(or_2_out), .Clear(Clear), .valor_retorno(4'b1001),
    .out_6(decrementador_2_out_6));  // open: Preset
  or or_2 (or_2_out, Enable, not_1_out);
  Multiplexer multiplexer_2 (
    .in0(button_2_out), .in1(comparator_2_eq), .out(multiplexer_2_out), .sel(Enable));  // open: en
  Button button_2 (.out(button_2_out));
  Comparator #(.width(4)) comparator_1 (.a(decrementador_2_out_6), .b(4'b1001), .eq(comparator_1_eq));  // open: gt, lt
  assign and_1_out = ~decrementador_1_out_6 & ~decrementador_2_out_6 & ~decrementador_3_out_6 & ~decrementador_4_out_6;  // AND_Gate and_1, 4 bits wide
  Hex_Digit_Display hex_digit_display_3 (.value(decrementador_3_out_6));  // open: dp
  Decrementador decrementador_3 (
    .Clock(multiplexer_3_out), .Enable(or_3_out), .Clear(Clear), .valor_retorno(4'b0101),
    .out_6(decrementador_3_out_6));  // open: Preset
  or or_3 (or_3_out, Enable, not_1_out);
  Multiplexer multiplexer_3 (
    .in0(button_3_out), .in1(comparator_4_eq), .out(multiplexer_3_out), .sel(Enable));  // open: en
  Button button_3 (.out(button_3_out));
  Comparator #(.width(4)) comparator_2 (.a(decrementador_3_out_6), .b(4'b0101), .eq(comparator_2_eq));  // open: gt, lt
  Comparator #(.width(4)) comparator_3 (.a(and_1_out), .b(4'b1111), .eq(comparator_3_eq));  // open: gt, lt
  Hex_Digit_Display hex_digit_display_4 (.value(decrementador_4_out_6));  // open: dp
  Decrementador decrementador_4 (
    .Clock(multiplexer_4_out), .Enable(or_4_out), .Clear(Clear), .valor_retorno(4'b1001),
    .out_6(decrementador_4_out_6));  // open: Preset
  or or_4 (or_4_out, Enable, not_1_out);
  Multiplexer multiplexer_4 (.in0(button_4_out), .in1(and_2_out), .out(multiplexer_4_out), .sel(Enable));  // open: en
  Button button_4 (.out(button_4_out));
  Comparator #(.width(4)) comparator_4 (.a(decrementador_4_out_6), .b(4'b1001), .eq(comparator_4_eq));  // open: gt, lt
  and and_2 (and_2_out, not_2_out, clock_1_out);
  Clock clock_1 (.out(clock_1_out));
  not not_2 (not_2_out, comparator_3_eq);
endmodule

module Entrada (
  input  A3,
  input  A2,
  input  A1,
  input  A0,
  output [3:0] resultado
);

  Hex_Digit_Display hex_digit_display_1 (.value({A3, A2, A1, A0}));  // open: dp

  assign resultado = {A3, A2, A1, A0};
endmodule

// coordenadas
module Coordenadas (
  input  [3:0] a,
  input  [3:0] b,
  input  proximo,
  input  chutar,
  output Jogador_A,
  output Jogador_B,
  output Acertou,
  output MAIOR,
  output IGUAL,
  output MENOR,
  output SX,
  output SY,
  output Chutando_Y,
  output Chutando_X,
  output [3:0] saidax,
  output [3:0] saiday
);

  wire and_1_out, and_2_out, and_3_out, and_4_out, and_5_out, and_6_out, comparator_1_eq, comparator_2_eq,
       comparator_4_eq, comparator_5_eq, comparator_8_eq, comparator_8_gt, comparator_8_lt, comparator_9_eq,
       comparator_10_eq;
  wire [3:0] adder_1_out, adder_2_out, flip_flop_condicao_1_valor_saida, flip_flop_condicao_2_valor_saida,
       flip_flop_condicao_3_valor_saida, flip_flop_condicao_4_valor_saida, multiplexer_1_out,
       multiplexer_2_out, random_1_out, random_2_out, register_1_q, register_2_q;

  Hex_Digit_Display hex_digit_display_1 (.value(flip_flop_condicao_1_valor_saida));  // open: dp
  flip_flop_condicao flip_flop_condicao_1 (
    .Clock(proximo), .Preset(1'b0), .Enable(1'b1), .Clear(1'b0), .valor_retorno(4'b0000),
    .valor_max__1(4'b0011), .valor_saida(flip_flop_condicao_1_valor_saida));
  Comparator #(.width(4)) comparator_1 (
    .a(flip_flop_condicao_1_valor_saida), .b(4'b0010), .eq(comparator_1_eq));  // open: gt, lt
  Comparator #(.width(4)) comparator_2 (
    .a(flip_flop_condicao_1_valor_saida), .b(4'b0000), .eq(comparator_2_eq));  // open: gt, lt
  flip_flop_condicao flip_flop_condicao_2 (
    .Clock(comparator_2_eq), .Enable(1'b1), .Clear(1'b0), .valor_retorno(4'b0000), .valor_max__1(4'b0010),
    .valor_saida(flip_flop_condicao_2_valor_saida));  // open: Preset
  Comparator #(.width(4)) comparator_3 (
    .a(flip_flop_condicao_2_valor_saida), .b(4'b0000), .eq(Jogador_B));  // open: gt, lt
  not not_1 (Jogador_A, Jogador_B);
  Comparator #(.width(4)) comparator_4 (
    .a(flip_flop_condicao_1_valor_saida), .b(4'b0000), .eq(comparator_4_eq));  // open: gt, lt
  Comparator #(.width(4)) comparator_5 (
    .a(flip_flop_condicao_1_valor_saida), .b(4'b0001), .eq(comparator_5_eq));  // open: gt, lt
  Comparator #(.width(4)) comparator_6 (
    .a(flip_flop_condicao_1_valor_saida), .b(4'b0000), .eq(Chutando_X));  // open: gt, lt
  Multiplexer #(.width(4)) multiplexer_1 (.in0(a), .in1(b), .out(multiplexer_1_out), .sel(Jogador_B));  // open: en
  and and_1 (and_1_out, comparator_4_eq, chutar);
  Hex_Digit_Display hex_digit_display_2 (.value(register_1_q));  // open: dp
  LED u_Chutando_X (.in(Chutando_X));
  Multiplexer #(.width(4)) multiplexer_2 (.in0(a), .in1(b), .out(multiplexer_2_out), .sel(Jogador_B));  // open: en
  Register #(.width(4)) register_1 (.D(multiplexer_1_out), .Q(register_1_q), .clk(and_1_out));  // open: en, clr
  and and_2 (and_2_out, chutar, comparator_5_eq);
  Comparator #(.width(4)) comparator_7 (
    .a(flip_flop_condicao_1_valor_saida), .b(4'b0001), .eq(Chutando_Y));  // open: gt, lt
  Register #(.width(4)) register_2 (.D(multiplexer_2_out), .Q(register_2_q), .clk(and_2_out));  // open: en, clr
  Hex_Digit_Display hex_digit_display_3 (.value(register_2_q));  // open: dp
  LED u_Chutando_Y (.in(Chutando_Y));
  and and_3 (and_3_out, comparator_2_eq, Acertou);
  Adder #(.width(4)) adder_1 (.a(register_1_q), .b(register_2_q), .out(adder_1_out));  // open: cin, cout
  numero_negativo numero_negativo_1 (
    .Entrada_3(register_1_q[3]), .Entrada_2(register_1_q[2]), .Entrada_1(register_1_q[1]),
    .Entrada_0(register_1_q[0]), .negativo(SX), .\Saída (saidax));
  Hex_Digit_Display hex_digit_display_4 (.value(random_1_out));  // open: dp
  Random #(.width(4)) random_1 (.clk(and_3_out), .out(random_1_out));  // open: next, clr
  Random #(.width(4)) random_2 (.clk(and_3_out), .out(random_2_out));  // open: next, clr
  Hex_Digit_Display hex_digit_display_5 (.value(random_2_out));  // open: dp
  numero_negativo numero_negativo_2 (
    .Entrada_3(register_2_q[3]), .Entrada_2(register_2_q[2]), .Entrada_1(register_2_q[1]),
    .Entrada_0(register_2_q[0]), .negativo(SY), .\Saída (saiday));
  Adder #(.width(4)) adder_2 (.a(random_1_out), .b(random_2_out), .out(adder_2_out));  // open: cin, cout
  and and_4 (and_4_out, Jogador_A, Acertou);
  and and_5 (and_5_out, Jogador_B, Acertou);
  Comparator #(.width(4)) comparator_8 (
    .a(adder_1_out), .b(adder_2_out), .gt(comparator_8_gt), .eq(comparator_8_eq), .lt(comparator_8_lt));
  flip_flop_condicao flip_flop_condicao_3 (
    .Clock(and_4_out), .Preset(1'b0), .Enable(1'b1), .Clear(1'b0), .valor_retorno(4'b0000),
    .valor_max__1(4'b1111), .valor_saida(flip_flop_condicao_3_valor_saida));
  flip_flop_condicao flip_flop_condicao_4 (
    .Clock(and_5_out), .Preset(1'b0), .Enable(1'b1), .Clear(1'b0), .valor_retorno(4'b0000),
    .valor_max__1(4'b1111), .valor_saida(flip_flop_condicao_4_valor_saida));
  Comparator #(.width(4)) comparator_9 (.a(register_1_q), .b(random_1_out), .eq(comparator_9_eq));  // open: gt, lt
  Comparator #(.width(4)) comparator_10 (.a(register_2_q), .b(random_2_out), .eq(comparator_10_eq));  // open: gt, lt
  Hex_Digit_Display hex_digit_display_6 (.value(flip_flop_condicao_3_valor_saida));  // open: dp
  Hex_Digit_Display hex_digit_display_7 (.value(flip_flop_condicao_4_valor_saida));  // open: dp
  and and_6 (and_6_out, comparator_9_eq, comparator_10_eq);
  LED A___B (.in(MAIOR));
  and and_7 (MAIOR, comparator_1_eq, comparator_8_gt);
  and and_8 (IGUAL, comparator_1_eq, comparator_8_eq);
  LED A____B (.in(IGUAL));
  LED A___B_2 (.in(MENOR));
  and and_9 (MENOR, comparator_1_eq, comparator_8_lt);
  and and_10 (Acertou, and_6_out, IGUAL);
endmodule

module flip_flop_condicao (
  input  Clock,
  input  Preset,
  input  Enable,
  input  Clear,
  input  [3:0] valor_retorno,
  input  [3:0] valor_max__1,
  output [3:0] valor_saida
);

  wire comparator_1_eq;
  wire [3:0] adder_1_out, multiplexer_1_out;

  Hex_Digit_Display hex_digit_display_1 (.value(valor_saida));  // open: dp
  Flip_Flop_SR flip_flop_sr_1 (
    .S_R(multiplexer_1_out[3]), .Clock(Clock), .Preset(Preset), .Enable(Enable), .Clear(Clear),
    .out_6(valor_saida[3]));
  Flip_Flop_SR flip_flop_sr_2 (
    .S_R(multiplexer_1_out[2]), .Clock(Clock), .Preset(Preset), .Enable(Enable), .Clear(Clear),
    .out_6(valor_saida[2]));
  Flip_Flop_SR flip_flop_sr_3 (
    .S_R(multiplexer_1_out[1]), .Clock(Clock), .Preset(Preset), .Enable(Enable), .Clear(Clear),
    .out_6(valor_saida[1]));
  Multiplexer #(.width(4)) multiplexer_1 (
    .in0(adder_1_out), .in1(valor_retorno), .out(multiplexer_1_out), .sel(comparator_1_eq));  // open: en
  Flip_Flop_SR flip_flop_sr_4 (
    .S_R(multiplexer_1_out[0]), .Clock(Clock), .Preset(Preset), .Enable(Enable), .Clear(Clear),
    .out_6(valor_saida[0]));
  Hex_Digit_Display hex_digit_display_2 (.value(adder_1_out));  // open: dp
  Adder #(.width(4)) adder_1 (.a(valor_saida), .b(4'b0001), .out(adder_1_out));  // open: cin, cout
  Comparator #(.width(4)) comparator_1 (.a(adder_1_out), .b(valor_max__1), .eq(comparator_1_eq));  // open: gt, lt
endmodule

module numero_negativo (
  input  Entrada_3,
  input  Entrada_2,
  input  Entrada_1,
  input  Entrada_0,
  output [3:0] \Saída ,
  output negativo
);

  wire [3:0] adder_1_out, not_1_out;

  Multiplexer #(.width(4)) multiplexer_1 (
    .in0({Entrada_3, Entrada_2, Entrada_1, Entrada_0}), .in1(adder_1_out), .out(\Saída ), .sel(Entrada_3));  // open: en
  Hex_Digit_Display hex_digit_display_1 (.value(\Saída ));  // open: dp
  assign not_1_out = ~{Entrada_3, Entrada_2, Entrada_1, Entrada_0};  // NOT_Gate not_1, 4 bits wide
  Adder #(.width(4)) adder_1 (.a(not_1_out), .b(4'b0001), .out(adder_1_out));  // open: cin, cout
  LED u_negativo (.in(Entrada_3));

  assign negativo = Entrada_3;
endmodule
